// Logisim project sdb88_lab7.circ as structural Verilog: 1 circuit, main circuit main
module main (
  input  [3:0] A,
  input  [3:0] B,
  input  Sub
);

  wire adder_1_cout, not_2_out, SOV, UOV, xor_2_out;
  wire [3:0] multiplexer_1_out, not_1_out, O;

  // Probe on A
  // Probe on B
  // Probe on O
  LED led_1 (.in(SOV));
  // Probe on A
  // Probe on B
  // Probe on O
  LED led_2 (.in(UOV));
  assign not_1_out = ~B;  // NOT_Gate not_1, 4 bits wide
  Adder #(.width(4)) adder_1 (.a(A), .b(multiplexer_1_out), .out(O), .cin(Sub), .cout(adder_1_cout));
  Multiplexer #(.width(4)) multiplexer_1 (.in0(B), .in1(not_1_out), .out(multiplexer_1_out), .sel(Sub));  // open: en
  // XOR_Gate xor_1 has open pins: in1=multiplexer_1_out[3], in3=A[3], out=open
  // NOT_Gate not_2 has open pins: in=open, out=not_2_out
  xor xor_2 (xor_2_out, A[3], O[3]);
  xor xor_3 (UOV, adder_1_cout, Sub);
  and and_1 (SOV, not_2_out, xor_2_out);
endmodule
